# Fritzing sketch Matrix (saved by Fritzing 0.9.3b)
breadboards: 1

parts:
  Part1 = Arduino Uno (Rev3)
  Part2 = Thumb Joystick
  Disp1 = LBT2088AH [part_number=LBT2088AH]
  U1 = MAX7219 [package=dil24]
  R1 = Resistor [tolerance=±5% resistance=15k package="2512 [SMD]"]
  R2 = Resistor [tolerance=±5% resistance=15k package="2512 [SMD]"]

nets:
  N1: Part1.A0, Part2.HORZ
  N2: Part1.D8, U1.LOAD
  N3: Part1.D11_PWM/MOSI, U1.DIN
  N4: Part1.D13/SCK, U1.CLK
  GND: Part1.GND, Part2.GND, U1.GND, U1.GND2
  VCC: Part1.5V, Part2.VCC, U1.VCC, R1.Pin_0
  N5: Disp1.pin1, U1.DIG4
  N6: Disp1.pin2, U1.DIG6
  N7: Disp1.pin_3, U1.SEGF
  N8: Disp1.pin_4, U1.SEGB
  N9: Disp1.pin_5, U1.DIG7
  N10: Disp1.pin_6, U1.SEGDP
  N11: Disp1.pin_7, U1.DIG5
  N12: Disp1.pin_8, U1.DIG2
  N13: Disp1.pin_9, U1.DIG0
  N14: Disp1.pin_10, U1.SEGC
  N15: Disp1.pin_11, U1.SEGE
  N16: Disp1.pin_12, U1.DIG3
  N17: Disp1.pin_13, U1.SEGD
  N18: Disp1.pin_14, U1.DIG1
  N19: Disp1.pin_15, U1.SEGA
  N20: Disp1.pin_16, U1.SEGG
  N21: U1.ISET, R2.Pin_1
  N22: R1.Pin_1, R2.Pin_0
